# Fritzing sketch wiring (saved by Fritzing 0.9.3b)

parts:
  Part3 = 16-Channel 12-bit PCA9685 PWM/Servo Driver
  J1 = Screw terminal - 2 pins [package=THT]
  MCU1 = Raspberry Pi Zero
  HC-SR04_Sensor_1 = HC-SR04 Ultrasonic Distance Sensor
  BATT1 = 4xAA Switchable Battery Pack w/Bare Wire

nets:
  N1: Part3.PWRIN, J1.pin1, BATT1.POS
  GND: Part3.GND, J1.pin2, MCU1.pin_6, MCU1.pin_20, MCU1.pin_34, MCU1.pin_39, HC-SR04_Sensor_1.GND, BATT1.NEG
  N2: Part3.VCC, MCU1.pin_1, MCU1.pin_17
  N3: Part3.SDA, MCU1.pin_3
  N4: Part3.SCL, MCU1.pin_5
  N5: MCU1.pin_2, MCU1.pin_4, HC-SR04_Sensor_1.VCC

custom parts:
  16-Channel 12-bit PCA9685 PWM/Servo Driver: The Adafruit 16-Channel 12-bit PWM/Servo Driver will drive up to 16 servos over I2C with only 2 pins. The on-board PCA9685 PWM controller will drive all 16 channels simultaneously with no additional processing overhead. What's more, you can chain up to 62 of them to control up to 992 servos - all with the same 2 pins
  4xAA Switchable Battery Pack w/Bare Wire: 4xAA Switchable Battery Pack with Bare Wire connection
